# Fritzing sketch doancoso (saved by Fritzing 0.9.9b)
circuit board: 29.5039cm x 11.2056cm
breadboards: 1

parts:
  Onderdeel1 = Arduino Uno (Rev3)
  LCM1602_IIC1 = LCM1602 IIC [part_number="LCM1602 IIC" chip_label="LCM1602 IIC" package="DIP (Dual Inline) [THT]"]
  LCD1 = LCD screen
  Part1 = RFID-RC522-v2
  M1 = fc-51 [package=THT]
  M2 = fc-51 [package=THT]
  M3 = fc-51 [package=THT]
  LED3 = smd LED [color="Red (633nm)" package="0603 [SMD]"]
  J2 = Basic Servo
  J3 = Piezo Speaker

nets:
  N1: Onderdeel1.A0, J3.pin2
  N2: Onderdeel1.A4/SDA, LCM1602_IIC1.SDA
  N3: Onderdeel1.A5/SCL, LCM1602_IIC1.SCL
  N4: Onderdeel1.D9_PWM, Part1.RST
  N5: Onderdeel1.D10_PWM/SS, Part1.SDA
  N6: Onderdeel1.D11_PWM/MOSI, Part1.MOSI
  N7: Onderdeel1.D12/MISO, Part1.MISO
  N8: Onderdeel1.D13/SCK, Part1.SCK
  GND: Onderdeel1.GND, LCM1602_IIC1.GND, Part1.GND, M1.pin2, M2.pin2, M3.pin2, LED3.cathode, J2.gnd
  N9: Onderdeel1.D2, J2.pulse
  N10: Onderdeel1.D4, M3.pin1
  N11: Onderdeel1.D5_PWM, M2.pin1
  N12: Onderdeel1.D6_PWM, M1.pin1
  N13: Onderdeel1.D7, LED3.anode
  3V3: Onderdeel1.3V3, Part1.3.3V
  VCC: Onderdeel1.5V, LCM1602_IIC1.VCC, M1.pin3, M2.pin3, M3.pin3, J2.vcc, J3.pin1
  VSS: LCM1602_IIC1.VSS, LCD1.VSS
  VDD: LCM1602_IIC1.VDD, LCD1.VDD
  N14: LCM1602_IIC1.V0, LCD1.V0
  N15: LCM1602_IIC1.RS, LCD1.RS
  N16: LCM1602_IIC1.RW, LCD1.R/W
  N17: LCM1602_IIC1.E, LCD1.E
  N18: LCM1602_IIC1.D0, LCD1.DB0
  N19: LCM1602_IIC1.D1, LCD1.DB1
  N20: LCM1602_IIC1.D2, LCD1.DB2
  N21: LCM1602_IIC1.D3, LCD1.DB3
  N22: LCM1602_IIC1.D4, LCD1.DB4
  N23: LCM1602_IIC1.D5, LCD1.DB5
  N24: LCM1602_IIC1.D6, LCD1.DB6
  N25: LCM1602_IIC1.D7, LCD1.DB7
  N26: LCM1602_IIC1.A, LCD1.LED+
  N27: LCM1602_IIC1.K, LCD1.LED-
  N28: LCM1602_IIC1.LED_A, LCM1602_IIC1.LED_B

custom parts:
  LCM1602 IIC: I2C-Module to use a 1602 or 2004 LCD on with the wire.h libory Serial LCD Modul
  RFID-RC522-v2: A simple China made RFID-RC522 Reader; do check the pin labels, as this is a MFRC522 based clone.

// code stored in the sketch: AnalogReadSerial2LCD_LED.ino
#include <Wire.h>
#include <LiquidCrystal_I2C.h>
#include <SPI.h>
#include <MFRC522.h>
#include <Servo.h>

#define SS_PIN 10
#define RST_PIN 9
#define SERVO_PIN 2
#define BUZZER_PIN A0
#define LED_PIN 7

// C?m bi?n h?ng ngo?i 3 v? trí
#define IR_SENSOR_1 4
#define IR_SENSOR_2 5
#define IR_SENSOR_3 6

MFRC522 mfrc522(SS_PIN, RST_PIN);
Servo servo;
LiquidCrystal_I2C lcd(0x27, 16, 2);

int availableSlots = 3;  // Ch? thay ??i khi qu?t th?
String parkedRFIDs[3] = {"", "", ""};  // L?u ID xe trong bãi

void setup() {
    Serial.begin(9600);
    SPI.begin();
    mfrc522.PCD_Init();
    servo.attach(SERVO_PIN);
    servo.write(0);  
    
    pinMode(BUZZER_PIN, OUTPUT);
    pinMode(LED_PIN, OUTPUT);
    pinMode(IR_SENSOR_1, INPUT);
    pinMode(IR_SENSOR_2, INPUT);
    pinMode(IR_SENSOR_3, INPUT);
    pinMode(LED_PIN, OUTPUT);
    lcd.init();
    lcd.backlight();
    lcd.setCursor(0, 0);
    lcd.print("VKU SmartParking");

    delay(2000);
    displayParkingStatus();
    
}

void loop() {

    displayParkingStatus();  

    if (mfrc522.PICC_IsNewCardPresent() && mfrc522.PICC_ReadCardSerial()) {
        String rfid = getRFID();
        lcd.clear();
        lcd.setCursor(0, 0);
        lcd.print("RFID: " + rfid);

        int index = findRFID(rfid);

        if (index != -1) {
            // ?? Xe r?i bãi ? availableSlots +1
            parkedRFIDs[index] = "";  
            availableSlots = min(availableSlots + 1, 3);  
            servo.write(90);  

            lcd.setCursor(2, 1);
            lcd.print("See you again!");
            buzzBuzzerTwice();
            delay(2000);
            
            displayAvailableSlots();
            servo.write(0);  
        } 
        else if (availableSlots > 0) {
            // ?? Xe vào ? availableSlots -1
            int emptyIndex = findEmptySlot();
            if (emptyIndex != -1) {
                parkedRFIDs[emptyIndex] = rfid;  
                availableSlots = max(availableSlots - 1, 0);  
                servo.write(90);  
                
                lcd.setCursor(4, 1);
                lcd.print("Welcome!");
                buzzBuzzerTwice();
                delay(2000);
                
                displayAvailableSlots();
                servo.write(0);  
            }
        }
        else {
            // ? Khi bãi ??y
            lcd.clear();
            lcd.setCursor(0, 0);
            lcd.print("Full slot!");
            
            buzzBuzzerLong();  
            delay(2000);
        }
    }

    delay(500);  
    digitalWrite(LED_PIN,HIGH); 
    delay(500);
    digitalWrite(LED_PIN,LOW);
    delay(500);
}

// ?? Hi?n th? tr?ng thái bãi ?? d?a vào c?m bi?n h?ng ngo?i
void displayParkingStatus() {
    lcd.clear();
    lcd.setCursor(0, 0);
    lcd.print("VKU SmartParking");

    lcd.setCursor(0, 1);
    lcd.print("S1:" + String(digitalRead(IR_SENSOR_1) == LOW ? "X " : "V "));
    lcd.print("S2:" + String(digitalRead(IR_SENSOR_2) == LOW ? "X " : "V "));
    lcd.print("S3:" + String(digitalRead(IR_SENSOR_3) == LOW ? "X " : "V "));
    
    delay(2000);
}

// ?? Hi?n th? s? ch? tr?ng sau khi qu?t th?
void displayAvailableSlots() {
    lcd.clear();
    lcd.setCursor(0, 0);
    lcd.print("Available: " + String(availableSlots) );

    delay(2000);
}

// ?? Tìm RFID trong danh sách xe ?ã ??
int findRFID(String rfid) {
    for (int i = 0; i < 3; i++) {
        if (parkedRFIDs[i] == rfid) {
            return i;
        }
    }
    return -1;
}

// ?? Tìm v? trí tr?ng ?? l?u RFID khi xe vào
int findEmptySlot() {
    for (int i = 0; i < 3; i++) {
        if (parkedRFIDs[i] == "") {
            return i;
        }
    }
    return -1;
}

// ??? L?y RFID t? th? qu?t
String getRFID() {
    String rfid = "";
    for (byte i = 0; i < mfrc522.uid.size; i++) {
        rfid.concat(String(mfrc522.uid.uidByte[i] < 0x10 ? "0" : ""));
        rfid.concat(String(mfrc522.uid.uidByte[i], HEX));
    }
    mfrc522.PICC_HaltA();
    return rfid;
}

// ?? Còi báo hi?u ng?n
void buzzBuzzer(unsigned int duration) {
    digitalWrite(BUZZER_PIN, HIGH);
    delay(duration);
    digitalWrite(BUZZER_PIN, LOW);
}

// ?? Còi kêu 2 l?n
void buzzBuzzerTwice() {
    for (int i = 0; i < 2; i++) {
        digitalWrite(BUZZER_PIN, HIGH);
        delay(100);
        digitalWrite(BUZZER_PIN, LOW);
        delay(300);
    }
}

// ?? Còi kêu dài khi bãi ??y
void buzzBuzzerLong() {
    digitalWrite(BUZZER_PIN, HIGH);
    delay(1500);  // Kêu 1.5 giây
    digitalWrite(BUZZER_PIN, LOW);
}
